// Logisim project 4 bit ALU with registers.circ as structural Verilog: 1 circuit, main circuit main
module main (
  input  [3:0] in_1,
  input  [1:0] in_2,
  input  [3:0] in_3,
  output [3:0] out_4
);

  wire and_1_out, clock_1_out, nand_1_out, nand_2_out, nand_3_out, nand_4_out, nand_5_out, nand_6_out,
       nand_7_out, nand_8_out, nand_9_out, nand_10_out, nand_11_out, nand_12_out, nand_13_out, nand_14_out,
       nand_15_out, nand_16_out, nand_17_out, nand_18_out, nand_19_out, nand_21_out, nand_22_out,
       nand_23_out, nand_24_out, nand_26_out, nand_33_out, nand_34_out, nand_35_out, nand_36_out,
       nand_37_out, nand_38_out, nand_39_out, nand_40_out, nand_41_out, nand_42_out, nand_43_out,
       nand_45_out, not_1_out, not_2_out, not_3_out;
  wire [3:0] adder_1_out, and_2_out, multiplexer_1_out, nand_27_out, nand_30_out, or_1_out, subtractor_1_out;

  Clock clock_1 (.out(clock_1_out));
  not not_1 (not_1_out, clock_1_out);
  not not_2 (not_2_out, not_1_out);
  not not_3 (not_3_out, not_2_out);
  and and_1 (and_1_out, clock_1_out, not_3_out);
  nand nand_1 (nand_1_out, in_1[0], and_1_out);
  nand nand_2 (nand_2_out, nand_1_out, and_1_out);
  nand nand_3 (nand_3_out, in_1[1], and_1_out);
  nand nand_4 (nand_4_out, nand_3_out, and_1_out);
  nand nand_5 (nand_5_out, in_1[2], and_1_out);
  nand nand_6 (nand_6_out, nand_5_out, and_1_out);
  nand nand_7 (nand_7_out, in_1[3], and_1_out);
  nand nand_8 (nand_8_out, nand_7_out, and_1_out);
  nand nand_9 (nand_9_out, in_3[0], and_1_out);
  nand nand_10 (nand_10_out, nand_9_out, and_1_out);
  nand nand_11 (nand_11_out, in_3[1], and_1_out);
  nand nand_12 (nand_12_out, nand_11_out, and_1_out);
  nand nand_13 (nand_13_out, in_3[2], and_1_out);
  nand nand_14 (nand_14_out, nand_13_out, and_1_out);
  nand nand_15 (nand_15_out, in_3[3], and_1_out);
  nand nand_16 (nand_16_out, nand_15_out, and_1_out);
  nand nand_17 (nand_17_out, nand_27_out[0], nand_2_out);
  nand nand_18 (nand_18_out, nand_27_out[1], nand_4_out);
  nand nand_19 (nand_19_out, nand_27_out[2], nand_6_out);
  nand nand_20 (nand_27_out[3], nand_7_out, nand_21_out);
  nand nand_21 (nand_21_out, nand_27_out[3], nand_8_out);
  nand nand_22 (nand_22_out, nand_30_out[0], nand_10_out);
  nand nand_23 (nand_23_out, nand_30_out[1], nand_12_out);
  nand nand_24 (nand_24_out, nand_30_out[2], nand_14_out);
  nand nand_25 (nand_30_out[3], nand_15_out, nand_26_out);
  nand nand_26 (nand_26_out, nand_30_out[3], nand_16_out);
  nand nand_27 (nand_27_out[0], nand_1_out, nand_17_out);
  nand nand_28 (nand_27_out[1], nand_3_out, nand_18_out);
  nand nand_29 (nand_27_out[2], nand_5_out, nand_19_out);
  nand nand_30 (nand_30_out[0], nand_9_out, nand_22_out);
  nand nand_31 (nand_30_out[1], nand_11_out, nand_23_out);
  nand nand_32 (nand_30_out[2], nand_13_out, nand_24_out);
  Adder #(.width(4)) adder_1 (.a(nand_27_out), .b(nand_30_out), .out(adder_1_out));  // open: cin, cout
  Subtractor #(.width(4)) subtractor_1 (.a(nand_27_out), .b(nand_30_out), .out(subtractor_1_out));  // open: bin, bout
  assign and_2_out = nand_27_out & nand_30_out;  // AND_Gate and_2, 4 bits wide
  assign or_1_out = nand_27_out | nand_30_out;  // OR_Gate or_1, 4 bits wide
  Multiplexer #(.select(2), .width(4), .enable("false")) multiplexer_1 (
    .in0(adder_1_out), .in1(subtractor_1_out), .in2(and_2_out), .in3(or_1_out), .out(multiplexer_1_out),
    .sel(in_2));
  nand nand_33 (nand_33_out, multiplexer_1_out[0], and_1_out);
  nand nand_34 (nand_34_out, nand_33_out, and_1_out);
  nand nand_35 (nand_35_out, multiplexer_1_out[1], and_1_out);
  nand nand_36 (nand_36_out, nand_35_out, and_1_out);
  nand nand_37 (nand_37_out, multiplexer_1_out[2], and_1_out);
  nand nand_38 (nand_38_out, nand_37_out, and_1_out);
  nand nand_39 (nand_39_out, multiplexer_1_out[3], and_1_out);
  nand nand_40 (nand_40_out, nand_39_out, and_1_out);
  nand nand_41 (nand_41_out, out_4[0], nand_34_out);
  nand nand_42 (nand_42_out, out_4[1], nand_36_out);
  nand nand_43 (nand_43_out, out_4[2], nand_38_out);
  nand nand_44 (out_4[3], nand_39_out, nand_45_out);
  nand nand_45 (nand_45_out, out_4[3], nand_40_out);
  nand nand_46 (out_4[0], nand_33_out, nand_41_out);
  nand nand_47 (out_4[1], nand_35_out, nand_42_out);
  nand nand_48 (out_4[2], nand_37_out, nand_43_out);
endmodule
